# Fritzing sketch LCD (saved by Fritzing 0.6.5b)
breadboards: 2

parts:
  Arduino5 = Arduino
  R9 = Resistor [tolerance=±5% resistance=1k package=THT]
  R10 = Resistor [tolerance=±5% resistance=220 package=THT]  # not connected
  LED7 = LED - 5mm [color="Red (633nm)" package="5 mm [THT]"]
  R11 = Photocell (LDR) [package=THT]

nets:
  N1: Arduino5.GND, R9.Pin_1, LED7.cathode
  N2: Arduino5.+5V, R11.pin_0
  N3: Arduino5.A1, R9.Pin_0, R11.pin_1
