# Fritzing sketch LED直接 (saved by Fritzing 0.6.5b)

parts:
  Arduino1 = Arduino
  LED1 = LED - 5mm [color="Red (633nm)" package="5 mm [THT]"]
  LED2 = LED - 5mm [color="Red (633nm)" package="5 mm [THT]"]  # not connected

nets:
  N1: Arduino1.GND, LED1.cathode
  N2: Arduino1.D13, LED1.anode
