# Fritzing sketch Processingに複数データを送る場合 (saved by Fritzing 0.6.5b)
breadboards: 1

parts:
  Arduino2 = Arduino
  J2 = Piezo Speaker
  RE1 = Rotary Encoder [package=THT]

nets:
  N1: Arduino2.GND, J2.pin1, RE1.EncoderPinA
  N2: Arduino2.D13, Arduino2.A0, J2.pin2
  N3: Arduino2.+5V, RE1.EncoderPinB
  N4: Arduino2.A1, RE1.EncoderPinC
