# Fritzing sketch ボタンスイッチ (saved by Fritzing 0.6.5b)
breadboards: 1

parts:
  Arduino3 = Arduino
  LED3 = LED - 5mm [color="Red (633nm)" package="5 mm [THT]"]
  R3 = Resistor [tolerance=±5% resistance=220 package=THT]
  S2 = Pushbutton [package="[THT]"]
  R4 = Resistor [tolerance=±5% resistance=10k package=THT]

nets:
  N1: Arduino3.GND, LED3.cathode, R4.Pin_1
  N2: Arduino3.D13, R3.Pin_1
  N3: Arduino3.D2, S2.Pin_1, S2.Pin_2, R4.Pin_0
  N4: Arduino3.+5V, S2.Pin_3, S2.Pin_4
  N5: LED3.anode, R3.Pin_0
