# Fritzing sketch 信号 (saved by Fritzing 0.6.5b)
breadboards: 1

parts:
  Arduino4 = Arduino
  LED4 = LED - 5mm [color="Red (633nm)" package="5 mm [THT]"]
  R5 = Resistor [tolerance=±5% resistance=220 package=THT]
  S3 = Pushbutton [package="[THT]"]
  R6 = Resistor [tolerance=±5% resistance=10k package=THT]
  LED5 = LED - 5mm [color="Blue (525nm)" package="5 mm [THT]"]
  LED6 = LED - 5mm [color="Yellow (592nm)" package="5 mm [THT]"]
  R7 = Resistor [tolerance=±5% resistance=220 package=THT]
  R8 = Resistor [tolerance=±5% resistance=220 package=THT]

nets:
  N1: Arduino4.GND, LED4.cathode, R6.Pin_1, LED5.cathode, LED6.cathode
  N2: Arduino4.D13, R8.Pin_1
  N3: Arduino4.D12, R7.Pin_1
  N4: Arduino4.D11, R5.Pin_1
  N5: Arduino4.D2, S3.Pin_1, S3.Pin_2, R6.Pin_0
  N6: Arduino4.+5V, S3.Pin_3, S3.Pin_4
  N7: LED4.anode, R5.Pin_0
  N8: LED5.anode, R8.Pin_0
  N9: LED6.anode, R7.Pin_0
