# Fritzing sketch 信号２ (saved by Fritzing 0.6.5b)
breadboards: 1

parts:
  Arduino5 = Arduino
  LED7 = LED - 5mm [color="Red (633nm)" package="5 mm [THT]"]
  S4 = Pushbutton [package="[THT]"]
  R10 = Resistor [tolerance=±5% resistance=10k package=THT]
  LED8 = LED - 5mm [color="Blue (525nm)" package="5 mm [THT]"]
  LED9 = LED - 5mm [color="Yellow (592nm)" package="5 mm [THT]"]
  R11 = Resistor [tolerance=±5% resistance=220 package=THT]

nets:
  N1: Arduino5.GND, R10.Pin_1, R11.Pin_1
  N2: Arduino5.D13, LED8.anode
  N3: Arduino5.D12, LED9.anode
  N4: Arduino5.D11, LED7.anode
  N5: Arduino5.D2, S4.Pin_1, S4.Pin_2, R10.Pin_0
  N6: Arduino5.+5V, S4.Pin_3, S4.Pin_4
  N7: LED7.cathode, LED8.cathode, LED9.cathode, R11.Pin_0
