# Fritzing sketch 圧電スピーカーで振動検知 (saved by Fritzing 0.6.5b)
breadboards: 1

parts:
  Arduino1 = Arduino
  J1 = Piezo Speaker
  LED1 = LED - 5mm [color="Red (633nm)" package="5 mm [THT]"]

nets:
  N1: Arduino1.GND, J1.pin1, LED1.cathode
  N2: Arduino1.D13, Arduino1.A0, J1.pin2
  N3: Arduino1.D6, LED1.anode
