# Fritzing sketch 温度センサー (saved by Fritzing 0.6.5b)
breadboards: 1

parts:
  Arduino1 = Arduino
  T1 = LM35 Temperature Sensor [package="TO92 [THT]"]

nets:
  N1: Arduino1.+5V, T1.+Vs
  GND: Arduino1.GND, T1.GND
  N2: Arduino1.A0, T1.Vout
