# Fritzing sketch 直列ボタン (saved by Fritzing 0.6.5b)
breadboards: 1

parts:
  Arduino2 = Arduino
  LED2 = LED - 5mm [color="Red (633nm)" package="5 mm [THT]"]
  R2 = Resistor [tolerance=±5% resistance=220 package=THT]
  S1 = Pushbutton [package="[THT]"]

nets:
  N1: Arduino2.GND, LED2.cathode
  N2: Arduino2.D13, S1.Pin_1, S1.Pin_2
  N3: LED2.anode, R2.Pin_0
  N4: R2.Pin_1, S1.Pin_3, S1.Pin_4
